# Fritzing sketch wiring schem (saved by Fritzing 0.9.3b)

parts:
  Part1 = Arduino Mega 2560 (Rev3)
  HC-SR04_Sensor_3 = HC-SR04 Ultrasonic Distance Sensor
  GY1 = MPU-6050 Board GY-521 [form="♀ (female)" package=THT]
  M1 = RioRand LM2596
  A1 = drv-1012
  J7 = Basic Servo
  M2 = DC Motor
  J9 = Camdenboss CTB0158-4 [part_number=CTB0158-4 package=THT]
  J10 = Camdenboss CTB0158-4 [part_number=CTB0158-4 package=THT]
  BAT1 = Battery Holders [package=lipo-1100mAh]
  HC-SR04_Sensor_8 = HC-SR04 Ultrasonic Distance Sensor
  HC-SR04_Sensor_9 = HC-SR04 Ultrasonic Distance Sensor
  HC-SR04_Sensor_10 = HC-SR04 Ultrasonic Distance Sensor
  HC-SR04_Sensor_11 = HC-SR04 Ultrasonic Distance Sensor
  HC-SR04_Sensor_12 = HC-SR04 Ultrasonic Distance Sensor
  BAT4 = Battery Holders [package=lipo-1100mAh]  # not connected
  BAT5 = Battery Holders [package=lipo-1100mAh]
  S2 = SWITCH-MOMENTARY-2 [package=tactile-pth]
  Raspberry_pi_4_model_b1 = IC, DIP package, 6 pins [chip_label="Raspberry pi 4 model b"]
  Raspberry_pi_camera_v_3 = IC, DIP package, 4 pins [chip_label="Raspberry pi camera v.2"]
  M3 = RioRand LM2596
  J11 = female alternating pin header, 1 pin [form="♀ (female)"]
  HC-SR04_Sensor_13 = HC-SR04 Ultrasonic Distance Sensor
  HC-SR04_Sensor_14 = HC-SR04 Ultrasonic Distance Sensor
  HC-SR04_Sensor_15 = HC-SR04 Ultrasonic Distance Sensor
  HC-SR04_Sensor_16 = HC-SR04 Ultrasonic Distance Sensor

nets (from the schematic view):
  N1: Part1.A9, A1.Pin_7
  N2: Part1.A10, A1.Pin_3
  N3: Part1.D21/SCL, Part1.SCL, GY1.pin4
  N4: Part1.D20/SDA, Part1.SDA, GY1.pin3
  GND: Part1.GND, HC-SR04_Sensor_3.ECHO, GY1.pin2, M1.Pin_4, J7.gnd, HC-SR04_Sensor_8.ECHO, HC-SR04_Sensor_9.ECHO, HC-SR04_Sensor_10.ECHO, HC-SR04_Sensor_11.ECHO, HC-SR04_Sensor_12.ECHO
  N5: Part1.D13_PWM, HC-SR04_Sensor_15.TRIG
  N6: Part1.D12_PWM, HC-SR04_Sensor_15.GND
  N7: Part1.D11_PWM, HC-SR04_Sensor_16.TRIG
  N8: Part1.D10_PWM, HC-SR04_Sensor_16.GND
  N9: Part1.D9_PWM, HC-SR04_Sensor_14.TRIG
  N10: Part1.D8_PWM, HC-SR04_Sensor_14.GND
  N11: Part1.D4_PWM, A1.Pin_8
  N12: Part1.D5_PWM, A1.Pin_4
  N13: Part1.D6_PWM, HC-SR04_Sensor_13.GND
  N14: Part1.D7_PWM, HC-SR04_Sensor_13.TRIG
  N15: Part1.D29, J7.pulse
  N16: Part1.D38, HC-SR04_Sensor_12.GND
  N17: Part1.D39, HC-SR04_Sensor_12.TRIG
  N18: Part1.D40, HC-SR04_Sensor_11.GND
  N19: Part1.D41, HC-SR04_Sensor_11.TRIG
  N20: Part1.D42, HC-SR04_Sensor_10.GND
  N21: Part1.D43, HC-SR04_Sensor_10.TRIG
  N22: Part1.D44, HC-SR04_Sensor_8.GND
  N23: Part1.D45, HC-SR04_Sensor_8.TRIG
  N24: Part1.D46, HC-SR04_Sensor_3.GND
  N25: Part1.D47, HC-SR04_Sensor_3.TRIG
  N26: Part1.D48, HC-SR04_Sensor_9.GND
  N27: Part1.D49, HC-SR04_Sensor_9.TRIG
  VCC: HC-SR04_Sensor_3.VCC, GY1.pin1, M1.Pin_3, J7.vcc, HC-SR04_Sensor_8.VCC, HC-SR04_Sensor_9.VCC, HC-SR04_Sensor_10.VCC, HC-SR04_Sensor_11.VCC, HC-SR04_Sensor_12.VCC, S2.2, HC-SR04_Sensor_13.VCC, HC-SR04_Sensor_14.VCC, HC-SR04_Sensor_15.VCC, HC-SR04_Sensor_16.VCC
  N28: M1.Pin_1, J10.pin4
  N29: M1.Pin_2, J9.pin1
  N30: A1.Pin_9, M2.pin_2
  N31: A1.Pin_10, M2.pin_1
  N32: A1.Pin_11, J9.pin3
  N33: A1.Pin_12, J10.pin2
  N34: J9.pin2, M3.Pin_4
  N35: J9.pin4, BAT5.+
  N36: J10.pin1, BAT1.-
  N37: J10.pin3, M3.Pin_3
  N38: Raspberry_pi_4_model_b1.pin1, M3.Pin_1
  N39: Raspberry_pi_4_model_b1.pin2, M3.Pin_2
  N40: Raspberry_pi_4_model_b1.pin3, J11.pin1
  N41: Raspberry_pi_4_model_b1.pin4, Raspberry_pi_camera_v_3.pin4
  N42: Raspberry_pi_4_model_b1.pin5, Raspberry_pi_camera_v_3.pin2
  N43: Raspberry_pi_4_model_b1.pin6, Raspberry_pi_camera_v_3.pin1

notes:
  serial port

custom parts:
  MPU-6050 Board GY-521: Acelerometro y Giroscopio MPU-6050 Board GY-521
  drv-1012: .The BTS7960 is a fully integrated high current H bridge module for motor drive applications.
