# Fritzing sketch wiring (saved by Fritzing 0.9.3b)

parts:
  Part1 = Arduino Mega 2560 (Rev3)
  HC-SR04_Sensor_3 = HC-SR04 Ultrasonic Distance Sensor
  GY1 = MPU-6050 Board GY-521 [form="♀ (female)" package=THT]
  M1 = RioRand LM2596
  A1 = drv-1012
  J7 = Basic Servo
  M2 = DC Motor
  J9 = Camdenboss CTB0158-4 [part_number=CTB0158-4 package=THT]
  J10 = Camdenboss CTB0158-4 [part_number=CTB0158-4 package=THT]
  Part4 = Arduino Mega Sensor Shield v2.0
  BAT1 = Battery Holders [package=lipo-1100mAh]
  HC-SR04_Sensor_8 = HC-SR04 Ultrasonic Distance Sensor
  HC-SR04_Sensor_9 = HC-SR04 Ultrasonic Distance Sensor
  HC-SR04_Sensor_10 = HC-SR04 Ultrasonic Distance Sensor
  HC-SR04_Sensor_11 = HC-SR04 Ultrasonic Distance Sensor
  HC-SR04_Sensor_12 = HC-SR04 Ultrasonic Distance Sensor
  BAT4 = Battery Holders [package=lipo-1100mAh]
  BAT5 = Battery Holders [package=lipo-1100mAh]
  M3 = RioRand LM2596
  F1 = Fan - Ventilador [package=THT]
  IC1 = Rasberry Pi NIOR Camera [chip_label=IC package="DIP (Dual Inline) [THT]"]  # not connected
  HC-SR04_Sensor_15 = HC-SR04 Ultrasonic Distance Sensor
  HC-SR04_Sensor_17 = HC-SR04 Ultrasonic Distance Sensor
  HC-SR04_Sensor_18 = HC-SR04 Ultrasonic Distance Sensor
  HC-SR04_Sensor_19 = HC-SR04 Ultrasonic Distance Sensor
  Raspberry_Pi_1 = Raspberry Pi 4 [part_number=RPI-4-b]  # not connected

nets:
  N1: Part1.A8, Part4.pin_8, Part4.pin_252
  N2: Part1.A9, Part4.pin_9, Part4.pin_255
  N3: Part1.A10, Part4.pin_10, Part4.pin_258
  N4: Part1.A11, Part4.pin_11, Part4.pin_261
  N5: Part1.A12, Part4.pin_12, Part4.pin_288
  N6: Part1.A13, Part4.pin_13, Part4.pin_291
  N7: Part1.A14, Part4.pin_14, Part4.pin_294
  N8: Part1.A15, Part4.pin_15, Part4.pin_297
  N9: Part1.A0, Part4.pin0, Part4.pin_180
  N10: Part1.A1, Part4.pin_1, Part4.pin_183
  N11: Part1.A2, Part4.pin_2, Part4.pin_186
  N12: Part1.A3, Part4.pin_3, Part4.pin_189
  N13: Part1.A4, Part4.pin_4, Part4.pin_216
  N14: Part1.A5, Part4.pin_5, Part4.pin_219
  N15: Part1.A6, Part4.pin_6, Part4.pin_222
  N16: Part1.A7, Part4.pin_7, Part4.pin_225
  N17: Part1.D21/SCL, GY1.pin3, Part4.pin_38, Part4.pin_273
  N18: Part1.D20/SDA, GY1.pin4, Part4.pin_39, Part4.pin_270
  N19: Part1.D19/RX1, Part4.pin_40, Part4.pin_267
  N20: Part1.D18/TX1, Part4.pin_41, Part4.pin_264
  N21: Part1.D17_PWM/RX2, Part4.pin_42, Part4.pin_237
  N22: Part1.D16_PWM/TX2, Part4.pin_43, Part4.pin_234
  N23: Part1.D15/RX3, Part4.pin_44, Part4.pin_231
  N24: Part1.D14/TX3, Part4.pin_45, Part4.pin_228
  N25: Part1.AREF, Part4.pin_37, Part4.pin_84
  GND: Part1.GND, HC-SR04_Sensor_3.GND, GY1.pin2, M1.Pin_4, A1.Pin_4, A1.Pin_8, J7.gnd, Part4.pin_19, Part4.pin_20, Part4.pin_36, Part4.pin_80, Part4.pin_81, Part4.pin_85, Part4.pin_97, Part4.pin_103, Part4.pin_106, Part4.pin_115, Part4.pin_130, Part4.pin_139, Part4.pin_148, Part4.pin_151, Part4.pin_163, Part4.pin_175, Part4.pin_181, Part4.pin_190, Part4.pin_193, Part4.pin_196, Part4.pin_202, Part4.pin_247, Part4.pin_271, Part4.pin_283, Part4.pin_326, HC-SR04_Sensor_8.GND, HC-SR04_Sensor_9.GND, HC-SR04_Sensor_10.GND, HC-SR04_Sensor_11.GND, HC-SR04_Sensor_12.GND, HC-SR04_Sensor_15.GND, HC-SR04_Sensor_17.GND, HC-SR04_Sensor_18.GND, HC-SR04_Sensor_19.GND
  N26: Part1.D13_PWM, Part4.pin_35, Part4.pin_90
  N27: Part1.D12_PWM, Part4.pin_34, Part4.pin_93
  N28: Part1.D11_PWM, Part4.pin_33, Part4.pin_120
  N29: Part1.D10_PWM, Part4.pin_32, Part4.pin_123
  N30: Part1.D9_PWM, Part4.pin_31, Part4.pin_126
  N31: Part1.D8_PWM, Part4.pin_30, Part4.pin_129
  N32: Part1.RESET, Part4.pin_16, Part4.pin_298
  N33: Part1.3V3, Part4.pin_17, Part4.pin_308
  N34: Part1.5V, Part4.pin_18, Part4.pin_46, Part4.pin_47, Part4.pin_303
  N35: Part1.VIN, Part4.pin_21
  N36: Part1.D0_RX0, Part4.pin_22, Part4.pin_201
  N37: Part1.D1_TX0, Part4.pin_23, Part4.pin_198
  N38: Part1.D2_PWM, Part4.pin_24, Part4.pin_195
  N39: Part1.D3_PWM, Part4.pin_25, Part4.pin_192
  N40: Part1.D4_PWM, J7.pulse, Part4.pin_26, Part4.pin_165
  N41: Part1.D5_PWM, Part4.pin_27, Part4.pin_162
  N42: Part1.D6_PWM, Part4.pin_28, Part4.pin_159
  N43: Part1.D7_PWM, Part4.pin_29, Part4.pin_156
  N44: Part1.D22, Part4.pin_48, Part4.pin_96, HC-SR04_Sensor_18.TRIG
  N45: Part1.D23, Part4.pin_49, Part4.pin_99, HC-SR04_Sensor_18.ECHO
  N46: Part1.D24, HC-SR04_Sensor_3.TRIG, Part4.pin_50, Part4.pin_102
  N47: Part1.D25, HC-SR04_Sensor_3.ECHO, Part4.pin_51, Part4.pin_105
  N48: Part1.D26, Part4.pin_52, Part4.pin_132
  N49: Part1.D27, Part4.pin_53, Part4.pin_135
  N50: Part1.D28, Part4.pin_54, Part4.pin_138, HC-SR04_Sensor_8.TRIG
  N51: Part1.D29, Part4.pin_55, Part4.pin_141, HC-SR04_Sensor_8.ECHO
  N52: Part1.D30, Part4.pin_56, Part4.pin_168
  N53: Part1.D31, Part4.pin_57, Part4.pin_171
  N54: Part1.D32, Part4.pin_58, Part4.pin_174, HC-SR04_Sensor_9.TRIG
  N55: Part1.D33, Part4.pin_59, Part4.pin_177, HC-SR04_Sensor_9.ECHO
  N56: Part1.D34, A1.Pin_6, A1.Pin_7, Part4.pin_60, Part4.pin_204
  N57: Part1.D35, A1.Pin_2, A1.Pin_3, Part4.pin_61, Part4.pin_207
  N58: Part1.D36, Part4.pin_62, Part4.pin_210
  N59: Part1.D37, Part4.pin_63, Part4.pin_213
  N60: Part1.D38, Part4.pin_64, Part4.pin_240
  N61: Part1.D39, Part4.pin_65, Part4.pin_243
  N62: Part1.D40, Part4.pin_66, Part4.pin_246, HC-SR04_Sensor_11.TRIG
  N63: Part1.D41, Part4.pin_67, Part4.pin_249, HC-SR04_Sensor_11.ECHO
  N64: Part1.D42, Part4.pin_68, Part4.pin_276
  N65: Part1.D43, Part4.pin_69, Part4.pin_279
  N66: Part1.D44, Part4.pin_70, Part4.pin_282, HC-SR04_Sensor_12.TRIG
  N67: Part1.D45, Part4.pin_71, Part4.pin_285, HC-SR04_Sensor_12.ECHO
  N68: Part1.D46, Part4.pin_72, Part4.pin_108, HC-SR04_Sensor_19.TRIG
  N69: Part1.D47, Part4.pin_73, Part4.pin_111, HC-SR04_Sensor_19.ECHO
  N70: Part1.D48, Part4.pin_74, Part4.pin_114, HC-SR04_Sensor_10.TRIG
  N71: Part1.D49, Part4.pin_75, Part4.pin_117, HC-SR04_Sensor_10.ECHO
  N72: Part1.D50, Part4.pin_76, Part4.pin_144, HC-SR04_Sensor_15.TRIG
  N73: Part1.D51, Part4.pin_77, Part4.pin_147, HC-SR04_Sensor_15.ECHO
  N74: Part1.D52, Part4.pin_78, Part4.pin_150, HC-SR04_Sensor_17.TRIG
  N75: Part1.D53, Part4.pin_79, Part4.pin_153, HC-SR04_Sensor_17.ECHO
  VCC: HC-SR04_Sensor_3.VCC, GY1.pin1, M1.Pin_3, J7.vcc, Part4.pin_98, Part4.pin_104, Part4.pin_107, Part4.pin_116, Part4.pin_131, Part4.pin_137, Part4.pin_140, Part4.pin_149, Part4.pin_152, Part4.pin_164, Part4.pin_176, Part4.pin_179, Part4.pin_191, Part4.pin_194, Part4.pin_248, Part4.pin_272, Part4.pin_284, Part4.pin_327, HC-SR04_Sensor_8.VCC, HC-SR04_Sensor_9.VCC, HC-SR04_Sensor_10.VCC, HC-SR04_Sensor_11.VCC, HC-SR04_Sensor_12.VCC, HC-SR04_Sensor_15.VCC, HC-SR04_Sensor_17.VCC, HC-SR04_Sensor_18.VCC, HC-SR04_Sensor_19.VCC
  N76: M1.Pin_1, J9.pin1
  N77: M1.Pin_2, J10.pin4
  N78: A1.Pin_9, M2.pin_2
  N79: A1.Pin_10, M2.pin_1
  N80: A1.Pin_11, J9.pin3
  N81: A1.Pin_12, J10.pin2
  N82: J9.pin2, M3.Pin_3
  N83: J9.pin4, BAT5.+
  N84: J10.pin1, BAT1.-
  N85: J10.pin3, M3.Pin_4
  N86: BAT1.+, BAT4.-
  N87: BAT4.+, BAT5.-
  N88: M3.Pin_1, F1.5V
  N89: M3.Pin_2, F1.GND

custom parts:
  MPU-6050 Board GY-521: Acelerometro y Giroscopio MPU-6050 Board GY-521
  drv-1012: .The BTS7960 is a fully integrated high current H bridge module for motor drive applications.
  Fan - Ventilador: Ventilador de 2 pines, se encuentra comunmente en computadoras de escritorio
  Rasberry Pi NIOR Camera: Camera
  Raspberry Pi 4: The RPi4, a faster version of the awesome Raspberry Pi 2 B ARM Board with 40 pin gpio. Ready for special Raspberry Pi B+ and RPi2 Hat (Hardware attached (on) top)
